// Logisim project ALU.circ as structural Verilog: 14 circuits, main circuit main
module main (
  input  [3:0] A,
  input  [3:0] B,
  input  [3:0] OP,
  output [3:0] Decimal,
  output [3:0] R,
  output Z_Flag,
  output S_Flag,
  output C_Flag
);

  wire [3:0] ALU_ADD_SUB, AND_4, LOR_2, NOT_4, OR_4, ROR_2, SHL_2, SHR_2, XOR_4;

  // NoConnect on B[3:2]
  ALU_AND alu_and_1 (.A(A), .B(B), .O(AND_4));
  ALU_OR alu_or_1 (.A(A), .B(B), .O(OR_4));
  ALU_XOR alu_xor_1 (.A(A), .B(B), .O(XOR_4));
  ALU_NOT alu_not_1 (.A(A), .O(NOT_4));
  ALU_LOR alu_lor_1 (.A(A), .Shift(B[1:0]), .O(LOR_2));
  ALU_ROR alu_ror_1 (.A(A), .Shift(B[1:0]), .O(ROR_2));
  ADD_SUB add_sub_1 (.Sel(OP[0]), .A(A), .B(B), .Carry(C_Flag), .O(ALU_ADD_SUB));
  ALU_SHL alu_shl_1 (.A(A), .Shift(B[1:0]), .O(SHL_2));  // open: CL
  ALU_SHR alu_shr_1 (.A(A), .Shift(B[1:0]), .O(SHR_2));  // open: CR
  // NoConnect on OP[1]
  // NoConnect on OP[2]
  // NoConnect on OP[3]
  Multiplexer #(.select(4), .width(4)) multiplexer_1 (
    .in0(AND_4), .in1(OR_4), .in2(XOR_4), .in3(LOR_2), .in4(ROR_2), .in5(NOT_4), .in6(ALU_ADD_SUB),
    .in7(ALU_ADD_SUB), .in8(SHL_2), .in9(SHR_2), .out(Decimal), .sel(OP));  // open: in10, in11, in12, in13, in14, in15
  nor nor_1 (Z_Flag, Decimal[0], Decimal[1], Decimal[2], Decimal[3]);

  assign R = Decimal;
  assign S_Flag = Decimal[3];

  // Other names for the same wires on the sheet: Shift[1:0] = B[1:0]; SEL = OP[0]

  // Notes on the sheet:
  //   ADD 0110
  //   AND  0000   
  //   OR 0001
  //   XOR 0010
  //   LOR 0011
  //   ROR 0100
  //   NOT 0101
  //   SUB 0111
  //   SHL 1000
  //   SHR 1001
endmodule

module FA (
  input  a,
  input  b,
  input  Cin,
  output S,
  output Cout
);

  wire and_1_out, and_2_out, xor_1_out;

  xor xor_1 (xor_1_out, a, b);
  xor xor_2 (S, xor_1_out, Cin);
  and and_1 (and_1_out, Cin, xor_1_out);
  and and_2 (and_2_out, a, b);
  or or_1 (Cout, and_1_out, and_2_out);
endmodule

module ALU_AND (
  input  [3:0] A,
  input  [3:0] B,
  output [3:0] O
);

  and and_1 (O[3], A[3], B[3]);
  and and_2 (O[2], A[2], B[2]);
  and and_3 (O[1], A[1], B[1]);
  and and_4 (O[0], A[0], B[0]);
endmodule

module ALU_OR (
  input  [3:0] A,
  input  [3:0] B,
  output [3:0] O
);

  or or_1 (O[3], A[3], B[3]);
  or or_2 (O[2], A[2], B[2]);
  or or_3 (O[1], A[1], B[1]);
  or or_4 (O[0], A[0], B[0]);
endmodule

module ALU_XOR (
  input  [3:0] A,
  input  [3:0] B,
  output [3:0] O
);

  xor xor_1 (O[3], A[3], B[3]);
  xor xor_2 (O[2], A[2], B[2]);
  xor xor_3 (O[1], A[1], B[1]);
  xor xor_4 (O[0], A[0], B[0]);
endmodule

module ALU_NOT (
  input  [3:0] A,
  output [3:0] O
);

  not not_1 (O[3], A[3]);
  not not_2 (O[2], A[2]);
  not not_3 (O[1], A[1]);
  not not_4 (O[0], A[0]);
endmodule

module ALU_LOR (
  input  [3:0] A,
  input  [1:0] Shift,
  output [3:0] O
);

  Multiplexer #(.select(2)) multiplexer_1 (.in0(A[3]), .in1(A[2]), .in2(A[1]), .in3(A[0]), .out(O[3]), .sel(Shift));
  Multiplexer #(.select(2)) multiplexer_2 (.in0(A[2]), .in1(A[1]), .in2(A[0]), .in3(A[3]), .out(O[2]), .sel(Shift));
  Multiplexer #(.select(2)) multiplexer_3 (.in0(A[1]), .in1(A[0]), .in2(A[3]), .in3(A[2]), .out(O[1]), .sel(Shift));
  Multiplexer #(.select(2)) multiplexer_4 (.in0(A[0]), .in1(A[3]), .in2(A[2]), .in3(A[1]), .out(O[0]), .sel(Shift));

  // Notes on the sheet:
  //   Left Rotate Circuit
endmodule

module ALU_ROR (
  input  [3:0] A,
  input  [1:0] Shift,
  output [3:0] O
);

  Multiplexer #(.select(2)) multiplexer_1 (.in0(A[3]), .in1(A[0]), .in2(A[1]), .in3(A[2]), .out(O[3]), .sel(Shift));
  Multiplexer #(.select(2)) multiplexer_2 (.in0(A[2]), .in1(A[3]), .in2(A[0]), .in3(A[1]), .out(O[2]), .sel(Shift));
  Multiplexer #(.select(2)) multiplexer_3 (.in0(A[1]), .in1(A[2]), .in2(A[3]), .in3(A[0]), .out(O[1]), .sel(Shift));
  Multiplexer #(.select(2)) multiplexer_4 (.in0(A[0]), .in1(A[1]), .in2(A[2]), .in3(A[3]), .out(O[0]), .sel(Shift));

  // Notes on the sheet:
  //   Right Rotate Circuit
endmodule

module ADD_SUB (
  input  Sel,
  input  [3:0] A,
  input  [3:0] B,
  output Carry,
  output [3:0] O
);

  wire fa_2_cout, fa_3_cout, fa_4_cout, xor_1_out, xor_2_out, xor_3_out, xor_4_out;

  xor xor_1 (xor_1_out, Sel, B[3]);
  FA fa_1 (.Cin(fa_2_cout), .a(xor_1_out), .b(A[3]), .S(O[3]), .Cout(Carry));
  xor xor_2 (xor_2_out, Sel, B[2]);
  FA fa_2 (.Cin(fa_3_cout), .a(xor_2_out), .b(A[2]), .S(O[2]), .Cout(fa_2_cout));
  xor xor_3 (xor_3_out, Sel, B[1]);
  FA fa_3 (.Cin(fa_4_cout), .a(xor_3_out), .b(A[1]), .S(O[1]), .Cout(fa_3_cout));
  xor xor_4 (xor_4_out, Sel, B[0]);
  FA fa_4 (.Cin(Sel), .a(xor_4_out), .b(A[0]), .S(O[0]), .Cout(fa_4_cout));
endmodule

module ALU_SHL (
  input  [3:0] A,
  input  [1:0] Shift,
  output [3:0] O,
  output CL
);

  Multiplexer #(.select(2)) multiplexer_1 (.in0(A[3]), .in1(A[2]), .in2(A[1]), .in3(A[0]), .out(O[3]), .sel(Shift));
  Multiplexer #(.select(2)) multiplexer_2 (.in0(A[2]), .in1(A[1]), .in2(A[0]), .in3(1'b0), .out(O[2]), .sel(Shift));
  Multiplexer #(.select(2)) multiplexer_3 (.in0(A[1]), .in1(A[0]), .in2(1'b0), .in3(1'b0), .out(O[1]), .sel(Shift));
  Multiplexer #(.select(2)) multiplexer_4 (.in0(A[0]), .in1(1'b0), .in2(1'b0), .in3(1'b0), .out(O[0]), .sel(Shift));
  Multiplexer #(.select(2)) multiplexer_5 (.in0(1'b0), .in1(A[3]), .in2(A[2]), .in3(A[1]), .out(CL), .sel(Shift));

  // Notes on the sheet:
  //   Left Shift
endmodule

module ALU_SHR (
  input  [3:0] A,
  input  [1:0] Shift,
  output [3:0] O,
  output CR
);

  Multiplexer #(.select(2)) multiplexer_1 (.in0(A[3]), .in1(1'b0), .in2(1'b0), .in3(1'b0), .out(O[3]), .sel(Shift));
  Multiplexer #(.select(2)) multiplexer_2 (.in0(A[2]), .in1(A[3]), .in2(1'b0), .in3(1'b0), .out(O[2]), .sel(Shift));
  Multiplexer #(.select(2)) multiplexer_3 (.in0(A[1]), .in1(A[2]), .in2(A[3]), .in3(1'b0), .out(O[1]), .sel(Shift));
  Multiplexer #(.select(2)) multiplexer_4 (.in0(A[0]), .in1(A[1]), .in2(A[2]), .in3(A[3]), .out(O[0]), .sel(Shift));
  Multiplexer #(.select(2)) multiplexer_5 (.in0(1'b0), .in1(A[0]), .in2(A[1]), .in3(A[2]), .out(CR), .sel(Shift));

  // Notes on the sheet:
  //   Right Shift
endmodule

module REG_1b (
  input  D_in,
  input  Sel,
  input  Clk,
  output D_out
);

  wire multiplexer_1_out;

  Multiplexer multiplexer_1 (.in0(D_out), .in1(D_in), .out(multiplexer_1_out), .sel(Sel));
  D_Flip_Flop REG_1B (.D(multiplexer_1_out), .clk(Clk), .Q(D_out));  // open: Qn, preset, reset
endmodule

module REG_4b (
  input  [3:0] D_in,
  input  Sel,
  input  Clk,
  output [3:0] D_out
);

  REG_1b b0 (.D_in(D_in[0]), .Sel(Sel), .Clk(Clk), .D_out(D_out[0]));
  REG_1b b1 (.D_in(D_in[1]), .Sel(Sel), .Clk(Clk), .D_out(D_out[1]));
  REG_1b b2 (.D_in(D_in[2]), .Sel(Sel), .Clk(Clk), .D_out(D_out[2]));
  REG_1b b3 (.D_in(D_in[3]), .Sel(Sel), .Clk(Clk), .D_out(D_out[3]));

  // Other names for the same wires on the sheet: D0 = D_in[0]; D1 = D_in[1]; D2 = D_in[2]; D3 = D_in[3];
  //   O0 = D_out[0]; O1 = D_out[1]; O2 = D_out[2]; O3 = D_out[3]
endmodule

module REG_FILE_4b (
  input  REG_EN,
  input  [2:0] Wr,
  input  [3:0] Wrd,
  input  Clk,
  input  [2:0] Ra,
  input  [2:0] Rb,
  output [3:0] A,
  output [3:0] B
);

  wire Reg0, Reg1, Reg2, Reg3, Reg4;
  wire [3:0] R0, R1, R2, R3, R4;

  Decoder #(.select(3)) decoder_1 (
    .out0(Reg0), .out1(Reg1), .out2(Reg2), .out3(Reg3), .out4(Reg4), .sel(Wr), .en(REG_EN));  // open: out5, out6, out7
  REG_4b u_R0 (.D_in(Wrd), .Sel(Reg0), .Clk(Clk), .D_out(R0));
  REG_4b u_R1 (.D_in(Wrd), .Sel(Reg1), .Clk(Clk), .D_out(R1));
  REG_4b u_R2 (.D_in(Wrd), .Sel(Reg2), .Clk(Clk), .D_out(R2));
  REG_4b u_R3 (.D_in(Wrd), .Sel(Reg3), .Clk(Clk), .D_out(R3));
  REG_4b u_R4 (.D_in(Wrd), .Sel(Reg4), .Clk(Clk), .D_out(R4));
  Multiplexer #(.select(3), .width(4)) multiplexer_1 (
    .in0(R0), .in1(R1), .in2(R2), .in3(R3), .in4(R4), .out(A), .sel(Ra));  // open: in5, in6, in7
  Multiplexer #(.select(3), .width(4)) multiplexer_2 (
    .in0(R0), .in1(R1), .in2(R2), .in3(R3), .in4(R4), .out(B), .sel(Rb));  // open: in5, in6, in7

  // Notes on the sheet:
  //   Design a 4 bit Register Set with 5 Registers
endmodule
