// Logisim project combinational.circ as structural Verilog: 7 circuits, main circuit main
module main (
);

  mux_4_1 mux_4_1_1 ();  // open: D3, D2, D1, D0, S1, S0, Y
  decoder_3_8 decoder_3_8_1 ();  // open: I1, I0, EN, I2, Y5, Y4, Y3, Y2, Y1, Y0, Y7, Y6
endmodule

module mux_2_1 (
  input  S,
  input  D1,
  input  D0,
  output Y
);

  wire and_1_out, and_2_out, not_1_out;

  not not_1 (not_1_out, S);
  and and_1 (and_1_out, not_1_out, D0);
  and and_2 (and_2_out, S, D1);
  or or_1 (Y, and_1_out, and_2_out);
endmodule

module mux_4_1 (
  input  S1,
  input  S0,
  input  D3,
  input  D2,
  input  D1,
  input  D0,
  output Y
);

  wire and_1_out, and_2_out, and_3_out, and_4_out, not_1_out, not_2_out;

  not not_1 (not_1_out, S1);
  not not_2 (not_2_out, S0);
  and and_1 (and_1_out, not_1_out, not_2_out, D0);
  and and_2 (and_2_out, not_1_out, S0, D1);
  and and_3 (and_3_out, S1, not_2_out, D2);
  and and_4 (and_4_out, S1, S0, D3);
  or or_1 (Y, and_1_out, and_2_out, and_3_out, and_4_out);
endmodule

module decoder_2_4 (
  input  I1,
  input  I0,
  output Y3,
  output Y2,
  output Y1,
  output Y0
);

  wire not_1_out, not_2_out;

  not not_1 (not_1_out, I1);
  not not_2 (not_2_out, I0);
  and and_1 (Y3, I1, I0);
  and and_2 (Y2, I1, not_2_out);
  and and_3 (Y1, not_1_out, I0);
  and and_4 (Y0, not_1_out, not_2_out);
endmodule

module decoder_3_8 (
  input  EN,
  input  I2,
  input  I1,
  input  I0,
  output Y7,
  output Y6,
  output Y5,
  output Y4,
  output Y3,
  output Y2,
  output Y1,
  output Y0
);

  wire not_1_out, not_2_out, not_3_out;

  not not_1 (not_1_out, I2);
  not not_2 (not_2_out, I1);
  not not_3 (not_3_out, I0);
  and and_1 (Y7, EN, I2, I1, I0);
  and and_2 (Y6, EN, I2, I1, not_3_out);
  and and_3 (Y5, EN, I2, not_2_out, I0);
  and and_4 (Y4, EN, I2, not_2_out, not_3_out);
  and and_5 (Y3, EN, not_1_out, I1, I0);
  and and_6 (Y2, EN, not_1_out, I1, not_3_out);
  and and_7 (Y1, EN, not_1_out, not_2_out, I0);
  and and_8 (Y0, EN, not_1_out, not_2_out, not_3_out);
endmodule

module encoder_4_2 (
  input  [7:0] A,
  output [2:0] Y
);

  wire not_1_out, not_2_out, not_3_out, not_4_out, not_5_out, not_6_out, not_7_out;

  not not_1 (not_1_out, A[6]);
  not not_2 (not_2_out, A[5]);
  not not_3 (not_3_out, A[4]);
  not not_4 (not_4_out, A[3]);
  not not_5 (not_5_out, A[2]);
  not not_6 (not_6_out, A[1]);
  not not_7 (not_7_out, A[0]);
  and and_1 (Y[2], not_4_out, not_5_out, not_6_out, not_7_out);
  and and_2 (Y[1], not_2_out, not_3_out, not_6_out, not_7_out);
  and and_3 (Y[0], not_1_out, not_3_out, not_5_out, not_7_out);
endmodule

module priority_encoder_8_3 (
  input  [7:0] A,
  output [2:0] Y,
  output Valid
);

  wire and_1_out, and_2_out, and_3_out, and_4_out, and_5_out, not_1_out, not_2_out, not_3_out, not_4_out;

  not not_1 (not_1_out, A[6]);
  not not_2 (not_2_out, A[5]);
  not not_3 (not_3_out, A[4]);
  not not_4 (not_4_out, A[2]);
  or or_1 (Y[2], A[4], A[5], A[6], A[7]);
  and and_1 (and_1_out, not_2_out, not_3_out, A[2]);
  and and_2 (and_2_out, not_2_out, not_3_out, A[3]);
  and and_3 (and_3_out, not_1_out, not_3_out, not_4_out, A[1]);
  and and_4 (and_4_out, not_1_out, not_3_out, A[3]);
  and and_5 (and_5_out, not_1_out, A[5]);
  or or_2 (Y[1], and_1_out, and_2_out, A[6], A[7]);
  or or_3 (Y[0], and_3_out, and_4_out, and_5_out, A[7]);

  assign Valid = A[0];
endmodule
